# Fritzing sketch fig_01-01 (saved by Fritzing 0.9.3b)
breadboards: 1

parts:
  Part1 = Arduino Uno (Rev3)
  R1 = Resistor [tolerance=±5% resistance=10k package=THT]
  LED1 = LED - 5mm [color="Red (633nm)" package="5 mm [THT]"]
  R2 = Resistor [tolerance=±5% resistance=330 package=THT]
  R3 = Photocell (LDR) [package=THT]

nets:
  N1: Part1.A0, R1.Pin_0, R3.pin_0
  N2: Part1.D9_PWM, R2.Pin_0
  GND: Part1.GND, R1.Pin_1, LED1.cathode
  5V: Part1.5V, R3.pin_1
  N3: LED1.anode, R2.Pin_1
